# Fritzing sketch Hardware-12v (saved by Fritzing 0.9.4)
stripboards: 1

parts:
  D1 = Rectifier Diode [part_number=1N4001 package="Melf DO-213 AB [SMD]"]  # not connected
  12V = female pin header, 2 pins [form="♀ (female)" part_number="JST-BEC female"]
  Ledstrip_12V = female pin header, 3 pins [form="♀ (female)" part_number="JST-SM Female"]
  Temp = female pin header, 2 pins [form="♀ (female)"]  # not connected
  Level = female pin header, 2 pins [form="♀ (female)"]  # not connected
  IRL540N = Basic FET N-Channel [package="D2Pak [SMD]"]

nets:
  N1: 12V.pin1, IRL540N.drain
  N2: 12V.pin2, Ledstrip_12V.pin3
  N3: Ledstrip_12V.pin1, IRL540N.source

notes:
  This is the 12V Ledstrip circuit
