# Fritzing sketch Hardware-5v (saved by Fritzing 0.9.4)
stripboards: 1

parts:
  D1 = Rectifier Diode [part_number=1N4001 package="Melf DO-213 AB [SMD]"]
  12V = female pin header, 2 pins [form="♀ (female)" part_number="JST-BEC female"]
  Ledstrip_5V = female pin header, 3 pins [form="♀ (female)" part_number="JST-SM Male"]
  Temp = female pin header, 2 pins [form="♀ (female)"]  # not connected
  Level = female pin header, 2 pins [form="♀ (female)"]  # not connected
  IRL540N = Basic FET N-Channel [package="D2Pak [SMD]"]

nets:
  N1: D1.anode, Ledstrip_5V.pin3
  N2: 12V.pin1, IRL540N.drain
  N3: 12V.pin2, IRL540N.source

notes:
  This is the 5V Ledstrip circuit
